# Fritzing sketch part1-single-led-5v (saved by Fritzing 0.9.2b)
breadboards: 1

parts:
  LED1 = LED - 5mm [color="Red (635nm)" package="5 mm [THT]"]  # not connected
  R1 = Resistor [tolerance=±5% resistance=220 package=THT]
  Raspberry_Pi1 = Raspberry Pi 2

nets:
  N1: R1.Pin_1, Raspberry_Pi1.GND
