# Fritzing sketch part2-single-led-gpio4 (saved by Fritzing 0.9.2b)
breadboards: 1

parts:
  Raspberry_Pi2 = Raspberry Pi 2
  LED2 = LED - 5mm [color="Red (635nm)" package="5 mm [THT]"]  # not connected
  R2 = Resistor [tolerance=±5% resistance=220 package=THT]

nets:
  N1: Raspberry_Pi2.GND, R2.Pin_1
