# Fritzing sketch part3-button-gpio4 (saved by Fritzing 0.9.2b)
breadboards: 1

parts:
  Raspberry_Pi1 = Raspberry Pi B rev2
  S1 = Pushbutton [package="[THT]"]
  R1 = Resistor [tolerance=±5% resistance=10k package=THT]

nets:
  N1: Raspberry_Pi1.5V, S1.Pin_3, S1.Pin_4
  N2: Raspberry_Pi1.GND, R1.Pin_1
  N3: Raspberry_Pi1.GPIO_4, S1.Pin_1, S1.Pin_2, R1.Pin_0
